# Fritzing sketch colorSensorFritz (saved by Fritzing 0.7.11b)
breadboards: 1

parts:
  Arduino1 = Arduino
  R1 = Photocell (LDR) [package=THT]
  R2 = Resistor [tolerance=±5% resistance=220 package=THT]
  LED1 = LED - 5mm [color="Red (633nm)" package="5 mm [THT]"]
  LED2 = LED - 5mm [color="Green (555nm)" package="5 mm [THT]"]
  LED3 = LED - 5mm [color="Blue (430nm)" package="5 mm [THT]"]
  R3 = Resistor [tolerance=±5% resistance=220 package=THT]
  R4 = Resistor [tolerance=±5% resistance=220 package=THT]
  R5 = Resistor [tolerance=±5% resistance=220 package=THT]

nets:
  N1: Arduino1.GND, R2.Pin_0, LED1.cathode, LED2.anode, LED3.anode
  N2: Arduino1.D4, R5.Pin_1
  N3: Arduino1.D3, R4.Pin_1
  N4: Arduino1.D2, R3.Pin_1
  N5: Arduino1.+5V, R1.pin_0
  N6: Arduino1.A0, R1.pin_1, R2.Pin_1
  N7: LED1.anode, R3.Pin_0
  N8: LED2.cathode, R4.Pin_0
  N9: LED3.cathode, R5.Pin_0
